# Fritzing sketch test (saved by Fritzing 0.9.3b)
circuit board: 5.07467cm x 3.52444cm
breadboards: 1

parts:
  R1 = Resistor [tolerance=±5% resistance=220 package=THT]
  C1 = Ceramic Capacitor [capacitance=100nF package="100 mil [THT, multilayer]"]
  S1 = Toggle Switch [package=THT]
  RE1 = Rotary Encoder [package=THT]
  RE2 = Hexadecimal Rotary Encoder [part_number=APEM-PT65-303 package=THT]
  T1 = LM35 Temperature Sensor [package="TO92 [THT]"]
  Part1 = Arduino Pro Mini v13
  MCU1 = Raspberry Pi Zero

nets:
  N1: R1.Pin_0, RE2.Output8pin
  N2: C1.1, S1.L1
  N3: S1.COM, RE1.EncoderPinA
  N4: S1.L2, RE2.Output1Pin, Part1.D6_PWM
  N5: RE1.EncoderPinB, T1.GND
  N6: RE2.Output4Pin, T1.Vout
  N7: RE2.InputCommon2, T1.+Vs
  N8: Part1.D2, MCU1.pin_13
  N9: Part1.RESET, MCU1.pin_3
